# Fritzing sketch arduino_pumpkin_Sketch (saved by Fritzing 0.8.3b)
breadboards: 1

parts:
  Part1 = Arduino Uno (Rev3)
  LED2 = LED - 5mm [color="Red (633nm)" package="5 mm [THT]"]
  C1 = Tantalum Capacitor [capacitance="1 μF" package="100 mil [THT, tantalum]"]
  Part2 = SRF05 Ultrasonic Rangefinder
  J1 = Piezo Speaker
  R1 = Resistor [tolerance=±5% resistance=220 package=THT]

nets:
  N1: Part1.ICSP_MISO, Part1.D12/MISO, Part2.connector10
  N2: Part1.ICSP_SCK, Part1.D13/SCK, Part2.connector9
  N3: Part1.ICSP_MOSI, Part1.D11_PWM/MOSI, C1.+
  N4: Part1.GND, LED2.cathode, C1.-, Part2.connector11, R1.Pin_1
  N5: Part1.D10_PWM/SS, LED2.anode
  N6: Part1.D4, J1.pin2
  N7: Part1.5V, Part2.connector8
  N8: J1.pin1, R1.Pin_0
